// Digital circuit CPU.dig as structural Verilog
module CPU (
  input  Clk,
  input  Clr
);

  wire CPU, HLT, IR, Mar, not_1_out, Out, PC, PC_ea, R_A, R_B, Zflag;
  wire [2:0] Bus_ea;
  wire [3:0] ir_1_q, ir_1_q_2, Opcode, ULA;
  wire [7:0] BUS, Mem, PC_out;

  not not_1 (not_1_out, HLT);
  and and_1 (CPU, not_1_out, Clk);
  Seven_Seg_Hex seven_seg_hex_1 (.d(ir_1_q_2), .dp(1'b0));
  pc pc_1 (.Bus(BUS), .Cp(PC_ea), .Ep(PC), .Clk(CPU), .Clr(Clr), .PC(PC_out));
  Seven_Seg_Hex seven_seg_hex_2 (.d(ir_1_q), .dp(1'b0));
  mem mem_1 (.Bus(BUS), .MAR(Mar), .Clk(CPU), .Clr(Clr), .Out(Mem));
  ir ir_1 (.NLi(BUS), .Clk(CPU), .NEi(Out), .Clr(Clr), .Q({ir_1_q_2, ir_1_q}));
  UC uc_1 (
    .Opcode(Opcode), .ZFlag_in(Zflag), .Clk(CPU), .Clr(Clr), .Bus(Bus_ea), .PC_ea(PC_ea), .PC(PC), .MAR(Mar),
    .IR(IR), .R_A(R_A), .R_B(R_B), .Out(Out), .ULA(ULA), .HLT(HLT));
  execution_unit execution_unit_1 (
    .Bus(BUS), .R_A(R_A), .R_B(R_B), .IR(IR), .ULA(ULA), .Bus_ea(Bus_ea), .Clk(CPU), .Clr(Clr), .Mem(Mem),
    .PC(PC_out), .Bus_Out(BUS), .Opcode(Opcode), .Z_flag(Zflag));

  // Notes on the sheet:
  //   Clk: Hz: 3
endmodule
