// Digital circuit UC.dig as structural Verilog
module UC (
  input  [3:0] Opcode,
  input  ZFlag_in,
  input  Clk,
  input  Clr,
  output [2:0] Bus,
  output PC_ea,
  output PC,
  output MAR,
  output IR,
  output R_A,
  output R_B,
  output Out,
  output [3:0] ULA,
  output HLT
);

  wire Add, and_1_out, and_2_out, and_3_out, and_4_out, and_5_out, and_6_out, and_7_out, Dec, Div, HLT_t,
       Inc, Jmp, Jmpz, LDA, Mult, or_2_out, or_3_out, or_4_out, Out1, Out2, Out3, Out4, Out5, Out_t, Sub, T1,
       T4, T5, T6;
  wire [2:0] priorityencoder_1_num;

  Decoder #(.Selector_Bits(4)) decoder_1 (
    .sel(Opcode), .out_0(Out1), .out_1(LDA), .out_2(Add), .out_3(Sub), .out_4(Mult), .out_5(Div),
    .out_6(Inc), .out_7(Dec), .out_8(Jmp), .out_9(Jmpz), .out_10(Out2), .out_11(Out3), .out_12(Out4),
    .out_13(Out5), .out_14(Out_t), .out_15(HLT_t));
  PriorityEncoder #(.Selector_Bits(3)) priorityencoder_1 (
    .in0(T1), .in1(PC_ea), .in2(IR), .in3(T4), .in4(T5), .in5(T6), .in6(1'b0), .in7(1'b0),
    .num(priorityencoder_1_num));  // open: any
  seq seq_1 (.Clk(Clk), .Clr(Clr), .T1(T1), .T2(PC_ea), .T3(IR), .T4(T4), .T5(T5), .T6(T6));
  and and_1 (and_1_out, Jmp, T4);
  and and_2 (and_2_out, Jmpz, ZFlag_in, T4);
  and and_3 (and_3_out, HLT_t, T4);
  or or_1 (PC, and_1_out, and_2_out);
  RS_FF_AS rs_ff_as_1 (.S(and_3_out), .R(Clr), .Q(HLT));  // open: nQ
  ROM #(.AddrBits(7), .Bits(7)) rom_1 (.A({Opcode, priorityencoder_1_num}), .sel(1'b1), .D({ULA, Bus}));
  or or_2 (or_2_out, LDA, Add, Sub, Mult, Div);
  and and_4 (and_4_out, LDA, T5);
  or or_3 (or_3_out, Sub, Add, Mult, Div);
  or or_4 (or_4_out, Dec, Inc);
  and and_5 (and_5_out, or_2_out, T4);
  and and_6 (and_6_out, or_3_out, T6);
  and and_7 (and_7_out, T4, or_4_out);
  or or_5 (MAR, and_5_out, T1);
  or or_6 (R_A, and_4_out, and_6_out, and_7_out);
  and and_8 (R_B, T5, or_3_out);
  and and_9 (Out, Out_t, T4);

  // Other names for the same wires on the sheet: HTL = HLT; MAR_ld = MAR; Out_ld = Out; T2 = PC_ea; T3 = IR;
  //   Zflag = ZFlag_in

  // Notes on the sheet:
  //   contents of rom_1 (hex, n*v repeats v):
  //   5,0,1,5*0,5,0,1,0,1,0,0,0,5,0,1,0,1,2,0,0,5,0,1,0,1,a,0,0,5,0
  //   ,1,0,1,1a,0,0,5,0,1,0,1,2a,0,0,5,0,1,32,4*0,5,0,1,3a,4*0,5,0,1
  //   ,5*0,5,0,1,37*0,5,0,1,3,4*0,5,0,1
endmodule
