// Digital circuit ULA.dig as structural Verilog
module ULA (
  input  [7:0] A,
  input  [7:0] B,
  input  [3:0] Op,
  output [7:0] RES,
  output Z
);

  wire [7:0] Add, Dec, Div, Inc, Mult, Sh, Sub;

  nor nor_1 (Z, RES[0], RES[1], RES[2], RES[3], RES[4], RES[5], RES[6], RES[7]);
  add8 add8_1 (.A(A), .B(B), .S(Add));  // open: Count
  sub8 sub8_1 (.B(A), .A(B), .Out(Sub));  // open: Neg
  incre incre_1 (.In(A), .Out(Inc));
  decre decre_1 (.In(A), .Out(Dec));
  shift_left shift_left_1 (.A(A), .S(Sh));
  div4 div4_1 (.D(A[3:0]), .d_2(B[3:0]), .q(Div[7:4]), .r(Div[3:0]));
  mult mult_1 (.A(A[3:0]), .B(B[3:0]), .S(Mult));
  Multiplexer #(.Selector_Bits(4), .Bits(8)) multiplexer_1 (
    .sel(Op), .in_0(Add), .in_1(Sub), .in_2(B), .in_3(Mult), .in_4(Sh), .in_5(Div), .in_6(Inc), .in_7(Dec),
    .in_8({8{1'b0}}), .in_9({8{1'b0}}), .in_10({8{1'b0}}), .in_11({8{1'b0}}), .in_12({8{1'b0}}),
    .in_13({8{1'b0}}), .in_14({8{1'b0}}), .in_15({8{1'b0}}), .out(RES));

  // Other names for the same wires on the sheet: AL[7:0] = RES; Zout = Z
endmodule
