// Digital circuit a.dig as structural Verilog
module a (
  input  A,
  input  B,
  input  Sel,
  output S
);

  wire add_1_s, sub_1_c_o;

  Add add_1 (.a(A), .b(B), .c_i(1'b0), .s(add_1_s));  // open: c_o
  Sub sub_1 (.a(A), .b(B), .c_i(1'b0), .c_o(sub_1_c_o));  // open: s
  Multiplexer multiplexer_1 (.sel(Sel), .in_0(add_1_s), .in_1(sub_1_c_o), .out(S));
endmodule
