// Digital circuit ac.dig as structural Verilog
module ac (
  input  NLa,
  input  Clk,
  input  Ea,
  input  [7:0] Input_Bus,
  output [7:0] Add_Sub,
  output [7:0] Out_Bus
);

  wire D0, D1, D2, D3, D4, D5, D6, D7, not_1_out;

  D_FF d_ff_1 (.D(D0), .C(Clk), .Q(Add_Sub[0]));  // open: nQ
  D_FF d_ff_2 (.D(D4), .C(Clk), .Q(Add_Sub[4]));  // open: nQ
  D_FF d_ff_3 (.D(D1), .C(Clk), .Q(Add_Sub[1]));  // open: nQ
  D_FF d_ff_4 (.D(D5), .C(Clk), .Q(Add_Sub[5]));  // open: nQ
  D_FF d_ff_5 (.D(D2), .C(Clk), .Q(Add_Sub[2]));  // open: nQ
  D_FF d_ff_6 (.D(D6), .C(Clk), .Q(Add_Sub[6]));  // open: nQ
  assign {D7, D6, D5, D4, D3, D2, D1, D0} = not_1_out ? Input_Bus : 8'bz;  // Driver driver_1
  not not_1 (not_1_out, NLa);
  assign Out_Bus = Ea ? Add_Sub : 8'bz;  // Driver driver_2
  D_FF d_ff_7 (.D(D3), .C(Clk), .Q(Add_Sub[3]));  // open: nQ
  D_FF d_ff_8 (.D(D7), .C(Clk), .Q(Add_Sub[7]));  // open: nQ

  // Other names for the same wires on the sheet: Q0 = Add_Sub[0]; Q1 = Add_Sub[1]; Q2 = Add_Sub[2]; Q3 = Add_Sub[3];
  //   Q4 = Add_Sub[4]; Q5 = Add_Sub[5]; Q6 = Add_Sub[6]; Q7 = Add_Sub[7]
endmodule
