// Digital circuit add4.dig as structural Verilog
module add4 (
  input  [3:0] A,
  input  [3:0] B,
  output [3:0] S,
  output Cout
);

  wire Cout1, Cout2, Cout3;

  // add add_1: pin names not known; wires that end beside it: A[0], B[0], 1'b0, S[0], Cout1
  // add add_2: pin names not known; wires that end beside it: A[1], B[1], Cout1, S[1], Cout2
  // add add_3: pin names not known; wires that end beside it: A[2], B[2], Cout2, S[2], Cout3
  // add add_4: pin names not known; wires that end beside it: A[3], B[3], Cout3, S[3], Cout
endmodule
