// Digital circuit add8.dig as structural Verilog
module add8 (
  input  [7:0] A,
  input  [7:0] B,
  output [7:0] S,
  output Count
);

  wire Cout1, Cout2, Cout3, Cout4, Cout5, Cout6, Cout7;

  // add add_1: pin names not known; wires that end beside it: A[0], B[0], 1'b0, S[0], Cout1
  // add add_2: pin names not known; wires that end beside it: A[1], B[1], Cout1, S[1], Cout2
  // add add_3: pin names not known; wires that end beside it: A[2], B[2], Cout2, S[2], Cout3
  // add add_4: pin names not known; wires that end beside it: A[3], B[3], Cout3, S[3], Cout4
  // add add_5: pin names not known; wires that end beside it: A[4], B[4], Cout4, S[4], Cout5
  // add add_6: pin names not known; wires that end beside it: A[5], B[5], Cout5, S[5], Cout6
  // add add_7: pin names not known; wires that end beside it: A[6], B[6], Cout6, S[6], Cout7
  // add add_8: pin names not known; wires that end beside it: A[7], B[7], Cout7, S[7], Count

  // Other names for the same wires on the sheet: dA0 = A[0]; dA1 = A[1]; dA2 = A[2]; dA3 = A[3]; dA4 = A[4];
  //   dA5 = A[5]; dA6 = A[6]; dA7 = A[7]; dB0 = B[0]; dB1 = B[1]; dB2 = B[2]; dB3 = B[3]; dB4 = B[4]; dB5 = B[5];
  //   dB6 = B[6]; dB7 = B[7]; dS0 = S[0]; dS1 = S[1]; dS2 = S[2]; dS3 = S[3]; dS4 = S[4]; dS5 = S[5]; dS6 = S[6];
  //   dS7 = S[7]
endmodule
