// Digital circuit decoder.dig as structural Verilog
module decoder (
  input  [3:0] Ins,
  output Lda,
  output Sub,
  output Out,
  output Hlt,
  output Sta,
  output Add,
  output Mul,
  output Div,
  output Inc,
  output Dec,
  output Jmp,
  output Jz,
  output Load
);

  wire nand_1_out, nand_2_out, nand_3_out, nand_4_out, nand_5_out, nand_6_out, nand_7_out, nand_8_out,
       nand_9_out, nand_10_out, nand_11_out, nand_12_out, NI4, NI5, NI6, NI7;

  not not_1 (NI4, Ins[3]);
  not not_2 (NI5, Ins[2]);
  not not_3 (NI6, Ins[1]);
  not not_4 (NI7, Ins[0]);
  nand nand_1 (nand_1_out, NI7, NI6, NI5, Ins[0]);
  nand nand_2 (nand_2_out, NI7, NI6, Ins[1], NI4);
  nand nand_3 (nand_3_out, NI7, NI6, Ins[1], Ins[0]);
  nand nand_4 (nand_4_out, NI7, Ins[2], NI5, NI4);
  nand nand_5 (nand_5_out, NI7, Ins[2], NI5, Ins[0]);
  not not_5 (Lda, nand_1_out);
  not not_6 (Sta, nand_2_out);
  not not_7 (Add, nand_3_out);
  not not_8 (Sub, nand_4_out);
  not not_9 (Mul, nand_5_out);
  nand nand_6 (nand_6_out, NI7, Ins[2], Ins[1], NI4);
  nand nand_7 (nand_7_out, NI7, Ins[2], Ins[1], Ins[0]);
  nand nand_8 (nand_8_out, Ins[3], NI6, NI5, NI4);
  nand nand_9 (nand_9_out, Ins[3], NI6, NI5, Ins[0]);
  not not_10 (Div, nand_6_out);
  not not_11 (Inc, nand_7_out);
  not not_12 (Dec, nand_8_out);
  not not_13 (Jmp, nand_9_out);
  nand nand_10 (nand_10_out, Ins[3], NI6, Ins[1], NI4);
  nand nand_11 (nand_11_out, Ins[3], NI6, Ins[1], Ins[0]);
  nand nand_12 (nand_12_out, Ins[3], Ins[2], Ins[1], NI4);
  nand nand_13 (Hlt, Ins[3], Ins[2], Ins[1], Ins[0]);
  not not_14 (Jz, nand_10_out);
  not not_15 (Load, nand_11_out);
  not not_16 (Out, nand_12_out);

  // Other names for the same wires on the sheet: I4 = Ins[0]; I5 = Ins[1]; I6 = Ins[2]; I7 = Ins[3]
endmodule
