// Digital circuit div4.dig as structural Verilog
module div4 (
  input  [3:0] D,
  input  [3:0] d_2,
  output [3:0] q,
  output [3:0] r
);

  wire nq0, nq1, nq2, nq3;
  wire [3:0] multiplexer_2_out, multiplexer_3_out, multiplexer_4_out, op0, op1, op2, op3, s0, s1, s2, s3;

  not not_1 (q[0], nq0);
  not not_2 (q[1], nq1);
  not not_3 (q[2], nq2);
  not not_4 (q[3], nq3);
  Multiplexer #(.Bits(4)) multiplexer_1 (.sel(nq0), .in_0(s0), .in_1(op0), .out(r));
  shift shift_1 (.In(4'b0000), .Shft(D[3]), .Out(op3));
  Multiplexer #(.Bits(4)) multiplexer_2 (.sel(nq3), .in_0(s3), .in_1(op3), .out(multiplexer_2_out));
  Multiplexer #(.Bits(4)) multiplexer_3 (.sel(nq2), .in_0(s2), .in_1(op2), .out(multiplexer_3_out));
  Multiplexer #(.Bits(4)) multiplexer_4 (.sel(nq1), .in_0(s1), .in_1(op1), .out(multiplexer_4_out));
  shift shift_2 (.In(multiplexer_2_out), .Shft(D[2]), .Out(op2));
  shift shift_3 (.In(multiplexer_3_out), .Shft(D[1]), .Out(op1));
  shift shift_4 (.In(multiplexer_4_out), .Shft(D[0]), .Out(op0));
  Sub #(.Bits(4)) sub_1 (.a(op3), .b(d_2), .c_i(1'b0), .s(s3), .c_o(nq3));
  Sub #(.Bits(4)) sub_2 (.a(op2), .b(d_2), .c_i(1'b0), .s(s2), .c_o(nq2));
  Sub #(.Bits(4)) sub_3 (.a(op1), .b(d_2), .c_i(1'b0), .s(s1), .c_o(nq1));
  Sub #(.Bits(4)) sub_4 (.a(op0), .b(d_2), .c_i(1'b0), .s(s0), .c_o(nq0));

  // Other names for the same wires on the sheet: d_t[3:0] = d_2
endmodule
