// Digital circuit execution_unit.dig as structural Verilog
module execution_unit (
  input  [7:0] Bus,
  input  R_A,
  input  R_B,
  input  IR,
  input  [3:0] ULA,
  input  [2:0] Bus_ea,
  input  Clk,
  input  Clr,
  input  [7:0] Mem,
  input  [7:0] PC,
  output [7:0] Bus_Out,
  output [3:0] Opcode,
  output Z_flag
);

  wire [3:0] Mux0;
  wire [7:0] Mux2, R_Aout, R_Bout;

  Register #(.Bits(8)) register_1 (.D(Bus), .C(Clk), .en(R_A), .Q(R_Aout));
  Register #(.Bits(8)) register_2 (.D(Bus), .C(Clk), .en(R_B), .Q(R_Bout));
  ULA ula_1 (.A(R_Aout), .B(R_Bout), .Op(ULA), .RES(Mux2), .Z(Z_flag));
  ir ir_1 (.NLi(Bus), .Clk(Clk), .NEi(IR), .Clr(Clr), .Q({Opcode, Mux0}));
  Multiplexer #(.Selector_Bits(3), .Bits(8)) multiplexer_1 (
    .sel(Bus_ea), .in_0({4'b0000, Mux0}), .in_1(Mem), .in_2(Mux2), .in_3(R_Aout), .in_4(R_Bout), .in_5(PC),
    .in_6({8{1'b0}}), .in_7({8{1'b0}}), .out(Bus_Out));

  // Other names for the same wires on the sheet: Mux1[7:0] = Mem; Mux3[7:0] = PC; Zflag = Z_flag
endmodule
