// Digital circuit fetch.dig as structural Verilog
module fetch (
  input  Clk,
  input  In,
  input  En,
  output [3:0] out_4
);

  wire _0, _1, _2, _3, _4, _5, and_1_out, and_2_out;
  wire [2:0] counter_1_out;

  Counter #(.Bits(3), .isProgramCounter("true")) counter_1 (
    .en(En), .C(In), .clr(and_1_out), .out(counter_1_out));  // open: ovf
  and and_1 (and_1_out, counter_1_out[0], counter_1_out[2]);
  and and_2 (and_2_out, En, ~counter_1_out[0], ~counter_1_out[1], ~counter_1_out[2]);  // And
  // ring_counter ring_counter_1: pin names not known; wires that end beside it: Clk, and_2_out, {_5, _4, _3, _2, _1, _0}
  assign out_4 = _0 ? 4'b0001 : 4'bz;  // Driver driver_1
  assign out_4 = _1 ? 4'b1000 : 4'bz;  // Driver driver_2
  assign out_4 = _2 ? 4'b1001 : 4'bz;  // Driver driver_3
  assign out_4 = _3 ? 4'b0110 : 4'bz;  // Driver driver_4
  assign out_4 = _4 ? 4'b0111 : 4'bz;  // Driver driver_5
  assign out_4 = _5 ? 4'b0010 : 4'bz;  // Driver driver_6
  decoder decoder_1 ();  // open: Ins, Lda, Sub, Out, Hlt, Sta, Add, Mul, Div, Inc, Dec, Jmp, Jz, Load
endmodule
