// Digital circuit full_add.dig as structural Verilog
module full_add (
  input  A,
  input  B,
  input  Ci,
  output S,
  output Carry
);

  wire CoA, CoB, half_add_1_s;

  half_add half_add_1 (.A(A), .B(B), .S(half_add_1_s), .Carry(CoA));
  or or_1 (Carry, CoA, CoB);
  half_add half_add_2 (.A(half_add_1_s), .B(Ci), .S(S), .Carry(CoB));

  // Other names for the same wires on the sheet: Co = Carry
endmodule
