// Digital circuit half_add.dig as structural Verilog
module half_add (
  input  A,
  input  B,
  output S,
  output Carry
);

  xor xor_1 (S, A, B);
  and and_1 (Carry, A, B);

  // Other names for the same wires on the sheet: AND = Carry; XOR = S
endmodule
