// Digital circuit ir.dig as structural Verilog
module ir (
  input  [7:0] NLi,
  input  Clk,
  input  NEi,
  input  Clr,
  output [7:0] Q
);

  wire [7:0] M;

  D_FF_AS #(.Bits(8)) d_ff_as_1 (.Set(1'b0), .D(M), .C(Clk), .Clr(Clr), .Q(Q));  // open: nQ
  Multiplexer #(.Bits(8)) multiplexer_1 (.sel(NEi), .in_0(Q), .in_1(NLi), .out(M));
endmodule
