// Digital circuit mult.dig as structural Verilog
module mult (
  input  [3:0] A,
  input  [3:0] B,
  output [7:0] S
);

  wire C1, C2, C2A, C3, C3A, C3B, C4, C4A, C4B, C5, CH2, S01, S02, S03, S3A, S4A, S10, S11, S12, S13, S20,
       S21, S22, S23, S30, S31, S32, S33, S_partial_2;

  and and_1 (S[0], A[0], B[0]);
  and and_2 (S10, A[1], B[0]);
  and and_3 (S20, A[2], B[0]);
  and and_4 (S30, A[3], B[0]);
  full_add F1 (.A(S32), .B(S23), .Ci(C4), .S(S[5]), .Carry(C5));
  half_add half_add_1 (.A(S10), .B(S01), .S(S[1]), .Carry(C1));
  or or_1 (C4, C4A, C4B);
  and and_5 (S01, A[0], B[1]);
  and and_6 (S11, A[1], B[1]);
  and and_7 (S21, A[2], B[1]);
  and and_8 (S31, A[3], B[1]);
  full_add F2 (.A(S31), .B(S22), .Ci(S13), .S(S4A), .Carry(C4A));
  half_add half_add_2 (.A(S33), .B(C5), .S(S[6]), .Carry(S[7]));
  or or_2 (C3, C3A, C3B);
  full_add F3 (.A(S30), .B(S21), .Ci(S12), .S(S3A), .Carry(C3A));
  and and_9 (S02, A[0], B[2]);
  and and_10 (S12, A[1], B[2]);
  and and_11 (S22, A[2], B[2]);
  and and_12 (S32, A[3], B[2]);
  half_add half_add_3 (.A(S4A), .B(C3), .S(S[4]), .Carry(C4B));
  or or_3 (C2, C2A, CH2);
  full_add F4 (.A(S3A), .B(S03), .Ci(C2), .S(S[3]), .Carry(C3B));
  and and_13 (S03, A[0], B[3]);
  and and_14 (S13, A[1], B[3]);
  and and_15 (S23, A[2], B[3]);
  and and_16 (S33, A[3], B[3]);
  half_add half_add_4 (.A(S_partial_2), .B(S02), .S(S[2]), .Carry(CH2));
  full_add F5 (.A(S20), .B(S11), .Ci(C1), .S(S_partial_2), .Carry(C2A));
endmodule
