// Digital circuit pc.dig as structural Verilog
module pc (
  input  [7:0] Bus,
  input  Cp,
  input  Ep,
  input  Clk,
  input  Clr,
  output [7:0] PC
);

  CounterPreset #(.Bits(8)) counterpreset_1 (
    .en(Cp), .C(Clk), .dir(1'b0), .in(Bus), .ld(Ep), .clr(Clr), .out(PC));  // open: ovf

  // Other names for the same wires on the sheet: RST = Clr
endmodule
