// Digital circuit ring_counter.dig as structural Verilog
module ring_counter (
  input  NCLR,
  input  CLK,
  output T1,
  output T2,
  output T3,
  output T4,
  output T5,
  output T6
);

  wire CLK_t, CLR, jk_ff_as_1_nq, jk_ff_as_2_nq, jk_ff_as_3_nq, jk_ff_as_4_nq, jk_ff_as_5_nq, NT6;

  not not_1 (CLK_t, CLK);
  not not_2 (CLR, NCLR);
  JK_FF_AS jk_ff_as_1 (.Set(1'b0), .J(NT6), .C(CLK_t), .K(T6), .Clr(CLR), .Q(T1), .nQ(jk_ff_as_1_nq));
  JK_FF_AS jk_ff_as_2 (.Set(1'b0), .J(jk_ff_as_1_nq), .C(CLK_t), .K(T1), .Clr(CLR), .Q(T2), .nQ(jk_ff_as_2_nq));
  JK_FF_AS jk_ff_as_3 (.Set(1'b0), .J(T2), .C(CLK_t), .K(jk_ff_as_2_nq), .Clr(CLR), .Q(T3), .nQ(jk_ff_as_3_nq));
  JK_FF_AS jk_ff_as_4 (.Set(1'b0), .J(T3), .C(CLK_t), .K(jk_ff_as_3_nq), .Clr(CLR), .Q(T4), .nQ(jk_ff_as_4_nq));
  JK_FF_AS jk_ff_as_5 (.Set(1'b0), .J(T4), .C(CLK_t), .K(jk_ff_as_4_nq), .Clr(CLR), .Q(T5), .nQ(jk_ff_as_5_nq));
  JK_FF_AS jk_ff_as_6 (.Set(1'b0), .J(T5), .C(CLK_t), .K(jk_ff_as_5_nq), .Clr(CLR), .Q(T6), .nQ(NT6));
endmodule
