// Digital circuit sub.dig as structural Verilog
module sub (
  input  [7:0] in_1,
  input  [7:0] in_2
);

  wire add8_1_count;
  wire [7:0] add8_1_s, add8_2_s, add8_3_p3, driver_1_out, not_1_out, not_2_out;

  assign not_1_out = ~in_2;  // Not not_1, 8 bits wide
  add8 add8_1 (.A(not_1_out), .B(8'h1), .S(add8_1_s), .Count(add8_1_count));
  add8 add8_2 (.A(in_1), .B(add8_1_s), .S(add8_2_s));  // open: Count
  LED led_1 (.in(add8_1_count));
  assign not_2_out = ~add8_2_s;  // Not not_2, 8 bits wide
  // add8 add8_3: pin names not known; wires that end beside it: not_2_out, 4'b0001, add8_3_p3
  assign driver_1_out = add8_2_s[7] ? add8_3_p3 : 8'bz;  // Driver driver_1
  assign driver_1_out = ~add8_2_s[7] ? add8_2_s : 8'bz;  // DriverInvSel driverinvsel_1
  Seven_Seg_Hex seven_seg_hex_1 (.d(driver_1_out[3:0]), .dp(add8_2_s[7]));
  // Pins of 4 and 8 bits meet at driver_1_out
endmodule
